// Logisim project part2.circ as structural Verilog: 1 circuit, main circuit my circuit
module my_circuit (
  input  [2:0] in_1,
  output out_2
);

  wire and_1_out;

  and and_1 (and_1_out, in_1[1], in_1[2]);
  or or_1 (out_2, in_1[0], and_1_out);

  // Other names for the same wires on the sheet: Output = out_2
endmodule
