// Logisim project hw3.circ as structural Verilog: 5 circuits, main circuit OneBitAdder
module OneBitAdder (
  input  A,
  input  B,
  input  Carryin,
  output Answer,
  output Carryout
);

  wire and_1_out, and_2_out, and_3_out, and_4_out, and_5_out, and_6_out, and_7_out;

  and and_1 (and_1_out, ~B, Carryin, ~A);  // AND_Gate
  and and_2 (and_2_out, B, ~Carryin, ~A);  // AND_Gate
  and and_3 (and_3_out, ~B, ~Carryin, A);  // AND_Gate
  and and_4 (and_4_out, B, Carryin, ~A);  // AND_Gate
  or or_1 (Answer, and_1_out, and_2_out, and_3_out, and_7_out);
  and and_5 (and_5_out, B, ~Carryin, A);  // AND_Gate
  or or_2 (Carryout, and_4_out, and_5_out, and_6_out, and_7_out);
  and and_6 (and_6_out, ~B, Carryin, A);  // AND_Gate
  and and_7 (and_7_out, B, Carryin, A);
endmodule

module FourBitAdder (
  input  [3:0] A,
  input  [3:0] B,
  input  Carryin,
  output [3:0] Answer,
  output Carryout
);

  wire onebitadder_2_carryout, onebitadder_3_carryout, onebitadder_4_carryout;

  OneBitAdder onebitadder_1 (
    .A(A[3]), .B(B[3]), .Carryin(onebitadder_2_carryout), .Answer(Answer[3]), .Carryout(Carryout));
  OneBitAdder onebitadder_2 (
    .A(A[2]), .B(B[2]), .Carryin(onebitadder_3_carryout), .Answer(Answer[2]),
    .Carryout(onebitadder_2_carryout));
  OneBitAdder onebitadder_3 (
    .A(A[1]), .B(B[1]), .Carryin(onebitadder_4_carryout), .Answer(Answer[1]),
    .Carryout(onebitadder_3_carryout));
  OneBitAdder onebitadder_4 (
    .A(A[0]), .B(B[0]), .Carryin(Carryin), .Answer(Answer[0]), .Carryout(onebitadder_4_carryout));
endmodule

module FourBitALU (
  input  [3:0] A,
  input  [3:0] B,
  input  S0,
  input  S1,
  input  S2,
  output [3:0] Output
);

  wire and_1_out, fourbitadder_3_p4;
  wire [0:0] isMultipleOf4;
  wire [3:0] _2_sComplementNegation, Addition, multiplyBy2, NAND, NOR, not_1_out, not_2_out, Subtraction, XOR;

  and and_1 (and_1_out, A[2], A[3]);
  assign XOR = A ^ B;  // XOR_Gate xor_1, 4 bits wide
  // FourBitAdder fourbitadder_1: pin names not known; wires that end beside it: A, B, 1'b0, Addition
  // FourBitAdder fourbitadder_2: pin names not known; wires that end beside it: A, 1'b0, multiplyBy2
  or or_1 (isMultipleOf4[0], ~A[0], ~A[1], A[2], A[3], and_1_out);  // OR_Gate
  assign not_1_out = ~B;  // NOT_Gate not_1, 4 bits wide
  assign NOR = ~(A | B);  // NOR_Gate nor_1, 4 bits wide
  // FourBitAdder fourbitadder_3: pin names not known; wires that end beside it: not_1_out, 4'b0001, 1'b0, fourbitadder_3_p4
  assign NAND = ~(A & B);  // NAND_Gate nand_1, 4 bits wide
  Multiplexer #(.select(3), .width(4), .disabled(0), .enable("false")) multiplexer_1 (
    .in0(Addition), .in1(Subtraction), .in2({3'b000, isMultipleOf4[0]}), .in3(_2_sComplementNegation),
    .in4(multiplyBy2), .in5(NAND), .in6(XOR), .in7(NOR), .out(Output), .sel({S2, S1, S0}));
  // FourBitAdder fourbitadder_4: pin names not known; wires that end beside it: A, fourbitadder_3_p4, 1'b0, Subtraction
  assign not_2_out = ~A;  // NOT_Gate not_2, 4 bits wide
  // FourBitAdder fourbitadder_5: pin names not known; wires that end beside it: not_2_out, 4'b0001, 1'b0, _2_sComplementNegation
endmodule

module SixteenBitAdder (
  input  [15:0] A,
  input  [15:0] B,
  input  CarryIn,
  output Carryout,
  output [15:0] Answer
);

  wire fourbitadder_1_p4, fourbitadder_2_p4, fourbitadder_3_p4;

  // FourBitAdder fourbitadder_1: pin names not known; wires that end beside it: A[3:0], B[3:0], CarryIn, fourbitadder_1_p4, Answer[3:0]
  // FourBitAdder fourbitadder_2: pin names not known; wires that end beside it: A[7:4], B[7:4], fourbitadder_1_p4, fourbitadder_2_p4, Answer[7:4]
  // FourBitAdder fourbitadder_3: pin names not known; wires that end beside it: A[11:8], B[11:8], fourbitadder_2_p4, fourbitadder_3_p4, Answer[11:8]
  // FourBitAdder fourbitadder_4: pin names not known; wires that end beside it: A[15:12], B[15:12], fourbitadder_3_p4, Carryout, Answer[15:12]

  // Other names for the same wires on the sheet: A0[3:0] = A[3:0]; A1[3:0] = A[7:4]; A2[3:0] = A[11:8];
  //   A3[3:0] = A[15:12]; B0[3:0] = B[3:0]; B1[3:0] = B[7:4]; B2[3:0] = B[11:8]; B3[3:0] = B[15:12]
endmodule

module SixteenBitALU (
  input  [15:0] A,
  input  [15:0] B,
  input  S0,
  input  S1,
  input  S2,
  output [15:0] Output
);

  wire [0:0] isMultipleOf4;
  wire [15:0] _2_sCOmplementNegation, Addition, NAND, NOR, not_1_out, not_2_out, sixteenbitadder_2_answer,
       Subtraction, XOR;

  SixteenBitAdder sixteenbitadder_1 (.CarryIn(1'b0), .A(A), .B(B), .Answer(Addition));  // open: Carryout
  assign XOR = A ^ B;  // XOR_Gate xor_1, 16 bits wide
  and and_1 (isMultipleOf4[0], A[0], A[1]);
  SixteenBitAdder sixteenbitadder_2 (
    .CarryIn(1'b0), .A(not_1_out), .B(16'h1), .Answer(sixteenbitadder_2_answer));  // open: Carryout
  assign not_1_out = ~A;  // NOT_Gate not_1, 16 bits wide
  SixteenBitAdder sixteenbitadder_3 (
    .CarryIn(1'b0), .A(sixteenbitadder_2_answer), .B(B), .Answer(Subtraction));  // open: Carryout
  assign NAND = ~(A & B);  // NAND_Gate nand_1, 16 bits wide
  assign NOR = ~(A | B);  // NOR_Gate nor_1, 16 bits wide
  Multiplexer #(.select(3), .width(16), .disabled(0), .enable("false")) multiplexer_1 (
    .in0(Addition), .in1(Subtraction), .in2({{15{1'b0}}, isMultipleOf4[0]}), .in3(_2_sCOmplementNegation),
    .in4({A[12:0], 3'b000}), .in5(NAND), .in6(NOR), .in7(XOR), .out(Output), .sel({S2, S1, S0}));
  assign not_2_out = ~A;  // NOT_Gate not_2, 16 bits wide
  SixteenBitAdder sixteenbitadder_4 (
    .CarryIn(1'b0), .A(not_2_out), .B(16'h1), .Answer(_2_sCOmplementNegation));  // open: Carryout

  // Other names for the same wires on the sheet: MultiplyBy8[15:3] = A[12:0]
endmodule
