// Logisim project hw4Part1.circ as structural Verilog: 1 circuit, main circuit my circuit
module my_circuit (
  input  CLK,
  input  K,
  input  RST,
  output A,
  output B,
  output C,
  output D
);

  wire and_1_out, and_2_out, and_3_out, and_4_out, and_5_out, and_6_out, and_7_out, and_8_out, and_9_out,
       not_1_out;
  wire [5:0] nor_1_out, register_1_q;

  and and_1 (and_1_out, register_1_q[3], ~K);  // AND_Gate
  or or_1 (nor_1_out[2], and_1_out, and_2_out);
  and and_2 (and_2_out, register_1_q[1], K);
  and and_3 (and_3_out, K, register_1_q[0]);
  or or_2 (nor_1_out[3], and_3_out, register_1_q[5], and_4_out);
  and and_4 (and_4_out, register_1_q[1], ~K);  // AND_Gate
  and and_5 (and_5_out, register_1_q[2], K);
  or or_3 (nor_1_out[4], and_5_out, and_6_out);
  and and_6 (and_6_out, register_1_q[4], K);
  or or_4 (nor_1_out[5], and_7_out, and_8_out, and_9_out);
  and and_7 (and_7_out, register_1_q[2], ~K);  // AND_Gate
  and and_8 (and_8_out, register_1_q[4], ~K);  // AND_Gate
  and and_9 (and_9_out, K, register_1_q[3]);
  not not_1 (not_1_out, K);
  and and_10 (nor_1_out[1], not_1_out, register_1_q[0]);
  nor nor_1 (nor_1_out[0], register_1_q[5], register_1_q[4], register_1_q[3], register_1_q[2], register_1_q[1], register_1_q[0]);
  Register #(.width(6)) register_1 (.D(nor_1_out), .en(1'b1), .Q(register_1_q), .clk(CLK), .clr(RST));
  or or_5 (A, register_1_q[0], register_1_q[2], register_1_q[4]);
  or or_6 (B, register_1_q[1], register_1_q[5]);
  or or_7 (C, register_1_q[2], register_1_q[3]);
  or or_8 (D, register_1_q[5], register_1_q[4]);

  // Notes on the sheet:
  //   Implement your state machine here
  //   Moving the input and output pins of this subcircuit will break the tester subcircuit
endmodule
