// Logisim project hw4Part2.circ as structural Verilog: 1 circuit, main circuit my circuit
module my_circuit (
  input  CLK,
  input  K,
  input  RST,
  output A,
  output B,
  output C,
  output D
);

  wire and_1_out, and_2_out, and_3_out, and_4_out, and_5_out, and_6_out, and_7_out, and_8_out, and_9_out,
       and_10_out, and_11_out;
  wire [0:0] register_1_q;
  wire [2:0] or_2_out;

  and and_1 (and_1_out, register_1_q[0], D);
  and and_2 (and_2_out, register_1_q[0], ~K);  // AND_Gate
  and and_3 (and_3_out, ~C, ~D, K);  // AND_Gate
  and and_4 (and_4_out, ~K, ~register_1_q[0]);  // AND_Gate
  and and_5 (and_5_out, ~C, ~K);  // AND_Gate
  or or_1 (or_2_out[1], and_1_out, and_2_out, and_3_out);
  and and_6 (and_6_out, ~register_1_q[0], D);  // AND_Gate
  and and_7 (and_7_out, ~D, ~C, ~register_1_q[0]);  // AND_Gate
  and and_8 (and_8_out, D, register_1_q[0]);
  or or_2 (or_2_out[0], and_5_out, and_4_out, and_8_out, and_7_out, and_11_out);
  or or_3 (or_2_out[2], and_6_out, and_9_out, and_10_out);
  and and_9 (and_9_out, ~register_1_q[0], C);  // AND_Gate
  and and_10 (and_10_out, K, C);
  and and_11 (and_11_out, K, C, register_1_q[0]);
  Register #(.width(3)) register_1 (.D(or_2_out), .Q({D, C, register_1_q[0]}), .clk(CLK), .clr(RST));  // open: en
  not not_1 (A, register_1_q[0]);
  and and_12 (B, register_1_q[0], ~C);  // AND_Gate

  // Notes on the sheet:
  //   Implement your state machine here
  //   Moving the input and output pins of this subcircuit will break the tester subcircuit
endmodule
