// Logisim project timedlab1.circ as structural Verilog: 3 circuits, main circuit my circuit
module my_circuit (
  input  [3:0] A,
  input  [3:0] B,
  input  [1:0] Select1,
  output [3:0] Output
);

  wire [3:0] nand_1_out, or_1_out, Times2, XNOR;

  assign or_1_out = A | B;  // OR_Gate or_1, 4 bits wide
  assign nand_1_out = ~(A & B);  // NAND_Gate nand_1, 4 bits wide
  Multiplexer #(.select(2), .width(4), .disabled(0), .enable("false")) multiplexer_1 (
    .in0({A[0], A[3:1]}), .in1({1'b0, A[2:0]}), .in2(XNOR), .in3(Times2), .out(Output), .sel(Select1));
  assign XNOR = nand_1_out & or_1_out;  // AND_Gate and_1, 4 bits wide
  _4BitAdder u_4bitadder_1 (.A(B), .B(B), .Carryin(1'b0), .out_5(Times2));  // open: Carryout

  // Other names for the same wires on the sheet: CircularRightshift[3:0] = {A[0], A[3:1]}; Mod8[2:0] = A[2:0]

  // Notes on the sheet:
  //   01 is Mod8 
  //   10 is XNOR
  //   00 is CircularRightShift
  //   11 is Times2
endmodule

module _1BitAdder (
  input  A,
  input  B,
  input  Carryin,
  output Answer,
  output Carryout
);

  wire and_1_out, and_2_out, and_3_out, and_4_out, and_5_out, and_6_out, and_7_out;

  and and_1 (and_1_out, ~B, Carryin, ~A);  // AND_Gate
  and and_2 (and_2_out, B, ~Carryin, ~A);  // AND_Gate
  and and_3 (and_3_out, ~B, ~Carryin, A);  // AND_Gate
  and and_4 (and_4_out, B, Carryin, ~A);  // AND_Gate
  or or_1 (Answer, and_1_out, and_2_out, and_3_out, and_7_out);
  and and_5 (and_5_out, B, ~Carryin, A);  // AND_Gate
  or or_2 (Carryout, and_4_out, and_5_out, and_6_out, and_7_out);
  and and_6 (and_6_out, ~B, Carryin, A);  // AND_Gate
  and and_7 (and_7_out, B, Carryin, A);
endmodule

module _4BitAdder (
  input  [3:0] A,
  input  [3:0] B,
  input  Carryin,
  output Carryout,
  output [3:0] out_5
);

  wire n1bitadder_2_carryout, n1bitadder_3_carryout, n1bitadder_4_carryout;

  _1BitAdder u_1bitadder_1 (
    .A(A[3]), .B(B[3]), .Carryin(n1bitadder_2_carryout), .Answer(out_5[3]), .Carryout(Carryout));
  _1BitAdder u_1bitadder_2 (
    .A(A[2]), .B(B[2]), .Carryin(n1bitadder_3_carryout), .Answer(out_5[2]), .Carryout(n1bitadder_2_carryout));
  _1BitAdder u_1bitadder_3 (
    .A(A[1]), .B(B[1]), .Carryin(n1bitadder_4_carryout), .Answer(out_5[1]), .Carryout(n1bitadder_3_carryout));
  _1BitAdder u_1bitadder_4 (.A(A[0]), .B(B[0]), .Carryin(Carryin), .Answer(out_5[0]), .Carryout(n1bitadder_4_carryout));

  // Notes on the sheet:
  //   Answer
endmodule
