// Logisim project Datapath2.circ as structural Verilog: 4 circuits, main circuit my circuit
module my_circuit (
);

  wire _1E, _2E, _3E, _4E, _5E, _6E, _7E, _8E, _9E, _10E, _11E, _12E, _13E, _14E, _15E, ALUHi, ALULo, C,
       CCMatch, DrALU, DrMEM, DrOFF, DrPC, DrReg, LdA, LdB, LdCC, LdIR, LdMAR, LdPC, RegSelHi, RegSelLo,
       WrMEM, WrReg;
  wire [2:0] comparator_1_gt, register_4_q;
  wire [3:0] R;
  wire [31:0] _1O, _2O, _3O, _4O, _5O, _6O, _7O, _8O, _9O, _10O, _11O, _12O, _13O, _14O, _15O, alu_1_out_4,
       bit_extender_1_out, D, IROut, MAR_q, PC_q, ram_1_data, register_3_q, register_6_q, RegOut;

  Clock Clock (.out(C));
  Register #(.width(32)) register_1 (.D(D), .en(_1E), .Q(_1O), .clk(C));  // open: clr
  Register #(.width(32)) PC (.D(D), .en(LdPC), .Q(PC_q), .clk(C));  // open: clr
  assign D = DrPC ? PC_q : 32'bz;  // Controlled_Buffer controlled_buffer_1
  Comparator #(.width(32)) comparator_1 (
    .a(D), .b({32{1'b0}}), .gt(comparator_1_gt[0]), .eq(comparator_1_gt[1]), .lt(comparator_1_gt[2]));
  Register #(.width(32)) register_2 (.D(D), .en(_2E), .Q(_2O), .clk(C));  // open: clr
  Register #(.width(32)) register_3 (.D(D), .en(LdA), .Q(register_3_q), .clk(C));  // open: clr
  ALU alu_1 (.A(register_3_q), .B(register_6_q), .Select({ALUHi, ALULo}), .out_4(alu_1_out_4));
  assign D = DrALU ? alu_1_out_4 : 32'bz;  // Controlled_Buffer controlled_buffer_2
  Register #(.width(3)) register_4 (.D(comparator_1_gt), .en(LdCC), .Q(register_4_q), .clk(C));  // open: clr
  Register #(.width(32)) register_5 (.D(D), .en(_3E), .Q(_3O), .clk(C));  // open: clr
  Multiplexer #(.select(4), .width(32), .disabled(0), .enable("false")) multiplexer_1 (
    .in0({32{1'b0}}), .in1(_1O), .in2(_2O), .in3(_3O), .in4(_4O), .in5(_5O), .in6(_6O), .in7(_7O), .in8(_8O),
    .in9(_9O), .in10(_10O), .in11(_11O), .in12(_12O), .in13(_13O), .in14(_14O), .in15(_15O), .out(RegOut),
    .sel(R));
  Register #(.width(32)) register_6 (.D(D), .en(LdB), .Q(register_6_q), .clk(C));  // open: clr
  CheckCC checkcc_1 (.CurrCC(register_4_q), .TestCC(IROut[22:20]), .CCMatch(CCMatch));
  Demultiplexer #(.select(4), .disabled(0), .enable("false")) demultiplexer_1 (
    .out1(_1E), .out2(_2E), .out3(_3E), .out4(_4E), .out5(_5E), .out6(_6E), .out7(_7E), .out8(_8E),
    .out9(_9E), .out10(_10E), .out11(_11E), .out12(_12E), .out13(_13E), .out14(_14E), .out15(_15E),
    .in(WrReg), .sel(R));  // open: out0
  Multiplexer #(.select(2), .width(4), .disabled(0), .enable("false")) multiplexer_2 (
    .in0(IROut[27:24]), .in1(IROut[23:20]), .in2(IROut[3:0]), .out(R), .sel({RegSelHi, RegSelLo}));  // open: in3
  assign D = DrReg ? RegOut : 32'bz;  // Controlled_Buffer controlled_buffer_3
  Register #(.width(32)) register_7 (.D(D), .en(_4E), .Q(_4O), .clk(C));  // open: clr
  Register #(.width(32)) register_8 (.D(D), .en(_5E), .Q(_5O), .clk(C));  // open: clr
  Register #(.width(32)) MAR (.D(D), .en(LdMAR), .Q(MAR_q), .clk(C));  // open: clr
  RAM #(.addrWidth(24), .dataWidth(32), .bus("separate")) ram_1 (
    .addr(MAR_q[23:0]), .din(D), .data(ram_1_data), .str(WrMEM), .clk(C));  // open: sel, ld, clr
  assign D = DrMEM ? ram_1_data : 32'bz;  // Controlled_Buffer controlled_buffer_4
  Register #(.width(32)) register_9 (.D(D), .en(_6E), .Q(_6O), .clk(C));  // open: clr
  Microcontroller microcontroller_1 (
    .CCMatch(CCMatch), .IRROM(IROut[31:28]), .Clock(C),
    .Control_Signals({ALUHi, ALULo, RegSelHi, RegSelLo, WrMEM, WrReg, LdCC, LdB, LdA, LdMAR, LdIR, LdPC, DrOFF, DrPC, DrALU, DrMEM, DrReg}));
  Register #(.width(32)) IR (.D(D), .en(LdIR), .Q(IROut), .clk(C));  // open: clr
  Register #(.width(32)) register_10 (.D(D), .en(_7E), .Q(_7O), .clk(C));  // open: clr
  assign bit_extender_1_out = {{12{IROut[19]}}, IROut[19:0]};  // Bit_Extender bit_extender_1
  assign D = DrOFF ? bit_extender_1_out : 32'bz;  // Controlled_Buffer controlled_buffer_5
  Register #(.width(32)) register_11 (.D(D), .en(_8E), .Q(_8O), .clk(C));  // open: clr
  Register #(.width(32)) register_12 (.D(D), .en(_9E), .Q(_9O), .clk(C));  // open: clr
  Register #(.width(32)) register_13 (.D(D), .en(_10E), .Q(_10O), .clk(C));  // open: clr
  Register #(.width(32)) register_14 (.D(D), .en(_11E), .Q(_11O), .clk(C));  // open: clr
  Register #(.width(32)) register_15 (.D(D), .en(_12E), .Q(_12O), .clk(C));  // open: clr
  Register #(.width(32)) register_16 (.D(D), .en(_13E), .Q(_13O), .clk(C));  // open: clr
  Register #(.width(32)) register_17 (.D(D), .en(_14E), .Q(_14O), .clk(C));  // open: clr
  Register #(.width(32)) register_18 (.D(D), .en(_15E), .Q(_15O), .clk(C));  // open: clr

  // Other names for the same wires on the sheet: RegNo[3:0] = R

  // Notes on the sheet:
  //   $at
  //   $v0
  //   $a0
  //   $a1
  //   $a2
  //   $t0
  //   $t1
  //   $t2
  //   $s0
  //   $s1
  //   $s2
  //   $k0
  //   $sp
  //   $fp
  //   $ra
endmodule

module ALU (
  input  [31:0] A,
  input  [31:0] B,
  input  [1:0] Select,
  output [31:0] out_4
);

  wire [31:0] A1, Add, NAND;

  Adder #(.width(32)) adder_1 (.a(A), .b(B), .out(Add), .cin(1'b0));  // open: cout
  Multiplexer #(.select(2), .width(32), .disabled(0), .enable("false")) multiplexer_1 (
    .in0(Add), .in1(NAND), .in2(A1), .out(out_4), .sel(Select));  // open: in3
  assign NAND = ~(A & B);  // NAND_Gate nand_1, 32 bits wide
  Adder #(.width(32)) adder_2 (.a(A), .b(32'h1), .out(A1), .cin(1'b0));  // open: cout

  // Other names for the same wires on the sheet: S[1:0] = Select
endmodule

module CheckCC (
  input  [2:0] CurrCC,
  input  [2:0] TestCC,
  output CCMatch
);

  wire and_1_out, and_2_out, and_3_out;

  and and_1 (and_1_out, CurrCC[0], TestCC[0]);
  and and_2 (and_2_out, CurrCC[1], TestCC[1]);
  and and_3 (and_3_out, CurrCC[2], TestCC[2]);
  or or_1 (CCMatch, and_1_out, and_2_out, and_3_out);

  // Other names for the same wires on the sheet: C0 = CurrCC[0]; C1 = CurrCC[1]; C2 = CurrCC[2]; T0 = TestCC[0];
  //   T1 = TestCC[1]; T2 = TestCC[2]
endmodule

module Microcontroller (
  input  CCMatch,
  input  [3:0] IRROM,
  input  Clock,
  output [16:0] Control_Signals
);

  wire [1:0] CCMatchEx, Select;
  wire [5:0] multiplexer_1_out, rom_1_data, rom_2_data, rom_3_data, State_Register_q;

  assign CCMatchEx = {{1{1'b0}}, CCMatch};  // Bit_Extender bit_extender_1
  ROM #(.addrWidth(6), .dataWidth(25)) rom_1 (
    .addr(State_Register_q), .data({Select, Control_Signals, rom_1_data}));  // open: sel
  Register #(.width(6)) State_Register (.D(multiplexer_1_out), .Q(State_Register_q), .clk(Clock));  // open: en, clr
  Multiplexer #(.select(2), .width(6), .disabled(0), .enable("false")) multiplexer_1 (
    .in0(rom_1_data), .in1(rom_3_data), .in2(rom_2_data), .out(multiplexer_1_out), .sel(Select));  // open: in3
  ROM #(.addrWidth(2), .dataWidth(6)) rom_2 (.addr(CCMatchEx), .data(rom_2_data));  // open: sel
  ROM #(.addrWidth(4), .dataWidth(6)) rom_3 (.addr(IRROM), .data(rom_3_data));  // open: sel

  // Other names for the same wires on the sheet: C = Clock; IR[3:0] = IRROM

  // Notes on the sheet:
  //   contents of rom_1 (hex, n*v repeats v):
  //   6201 1082 c00900 84044 108045 30100 84047 8408 30100 8404a 10804b 230100 1000000 420e 840f 900 20211
  //   80840 84053 8414 2115 30080 4217 8418 30100 8405a 841b 211c 40040 1d
  //   contents of rom_2 (hex, n*v repeats v):
  //   0 d
  //   contents of rom_3 (hex, n*v repeats v):
  //   3 6 9 c 10 12 16 19 7*0 1d
endmodule
