// Logisim project LC3-2200b.circ as structural Verilog: 8 circuits, main circuit main
module main (
);

  wire and_1_out, and_2_out, Clock, comparator_1_eq, comparator_3_eq, comparator_4_eq, comparator_5_eq,
       comparator_6_eq, comparator_7_eq, comparator_8_eq, comparator_9_eq, not_1_out, not_2_out, or_3_out,
       RegSelA, RegSelB, Save, Stall, StallA, StallB, WB_Control, WrMEM;
  wire [1:0] comparator_2_eq, Condition, Func;
  wire [2:0] ex_mem_buffer_1_control_2;
  wire [3:0] EX_Opcode, EX_Rx, ID_Opcode, ID_Ry, ID_Rz, IF_Opcode, MEM_Opcode, MEM_Rx, WB_Opcode, WB_Rx;
  wire [6:4] rom_1_data;
  wire [27:0] IF_ir_2, ram_1_data;
  wire [31:0] adder_1_out, Branch, controlled_buffer_1_out, ex_mem_buffer_1_b_2, ex_mem_buffer_1_result_2,
       EX_Result, ID_A, ID_B, ID_Imm, ID_PC, idrr_ex_buffer_1_a_2, idrr_ex_buffer_1_bout,
       idrr_ex_buffer_1_imm_2, idrr_ex_buffer_1_pc_2, MEM_Result, multiplexer_3_out, multiplexer_4_out, NPC,
       OUT1, OUT2, PC_q, WB_Result;

  Clock clock_1 (.out(Clock));
  Register #(.width(32)) PC (.D(NPC), .en(1'b1), .Q(PC_q), .clk(Clock), .clr(1'b0));
  Adder #(.width(32)) adder_1 (.a(32'h1), .b(PC_q), .out(adder_1_out));  // open: cin, cout
  Data_Forward_Unit DFU (
    .WB_Data(WB_Result), .ID_Data(OUT1), .EX_Opcode(EX_Opcode), .MEM_Opcode(MEM_Opcode),
    .WB_Opcode(WB_Opcode), .MEM_Data(MEM_Result), .EX_Data(EX_Result), .ID_SR(ID_Ry), .EX_DR(EX_Rx),
    .MEM_DR(MEM_Rx), .WB_DR(WB_Rx), .Result(ID_A), .Stall(StallA));
  Data_Forward_Unit DFU_2 (
    .WB_Data(WB_Result), .ID_Data(OUT2), .EX_Opcode(EX_Opcode), .MEM_Opcode(MEM_Opcode),
    .WB_Opcode(WB_Opcode), .MEM_Data(MEM_Result), .EX_Data(EX_Result), .ID_SR(ID_Rz), .EX_DR(EX_Rx),
    .MEM_DR(MEM_Rx), .WB_DR(WB_Rx), .Result(ID_B), .Stall(StallB));
  Multiplexer #(.select(2), .width(32), .enable("false")) multiplexer_1 (
    .in0(adder_1_out), .in1(ID_A), .in2(Branch), .in3(PC_q), .out(NPC), .sel(Condition));
  RAM #(.addrWidth(24), .dataWidth(32)) ram_1 (
    .addr(PC_q[23:0]), .data({IF_Opcode, ram_1_data}), .clk(Clock), .ld(1'b1), .clr(1'b0));  // open: sel
  IF_IDRR_Buffer IF (
    .PC(adder_1_out), .IR({IF_Opcode, ram_1_data}), .PC_2(ID_PC),
    .IR_2({ID_Opcode, IF_ir_2[27:24], ID_Ry, IF_ir_2[19:0]}), .Clock(Clock), .Reset(1'b0), .Stall(Save));
  assign ID_Imm = {{12{IF_ir_2[19]}}, IF_ir_2[19:0]};  // Bit_Extender bit_extender_1
  Multiplexer #(.width(4), .enable("false")) multiplexer_2 (
    .in0(IF_ir_2[3:0]), .in1(IF_ir_2[27:24]), .out(ID_Rz), .sel(or_3_out));
  Comparator #(.width(4)) comparator_1 (.a(4'b1111), .b(ID_Opcode), .eq(comparator_1_eq));  // open: gt, lt
  Comparator #(.width(4)) comparator_2 (.a(4'b0100), .b(ID_Opcode), .eq(comparator_2_eq[0]));  // open: gt, lt
  Comparator #(.width(4)) comparator_3 (.a(4'b0011), .b(ID_Opcode), .eq(comparator_3_eq));  // open: gt, lt
  Comparator #(.width(32)) comparator_4 (.a(ID_A), .b(ID_B), .eq(comparator_4_eq));  // open: gt, lt
  Comparator #(.width(4)) comparator_5 (.a(ID_Opcode), .b(4'b1001), .eq(comparator_5_eq));  // open: gt, lt
  Comparator #(.width(4)) comparator_6 (.a(ID_Opcode), .b(4'b0111), .eq(comparator_6_eq));  // open: gt, lt
  // Probe on ID_Opcode
  // Probe on EX_Opcode
  // Probe on MEM_Opcode
  // Probe on WB_Opcode
  IDRR_EX_Buffer idrr_ex_buffer_1 (
    .Opcode(ID_Opcode), .Rx(IF_ir_2[27:24]), .PC(ID_PC), .Imm(ID_Imm), .A(ID_A), .Bin(ID_B),
    .Opcode_2(EX_Opcode), .Rx_2(EX_Rx), .PC_2(idrr_ex_buffer_1_pc_2), .Imm_2(idrr_ex_buffer_1_imm_2),
    .A_2(idrr_ex_buffer_1_a_2), .Bout(idrr_ex_buffer_1_bout), .Clock(Clock), .Reset(1'b0), .Stall(1'b0));
  or or_1 (Stall, StallA, StallB, comparator_1_eq);
  and and_1 (and_1_out, comparator_3_eq, comparator_4_eq);
  or or_2 (comparator_2_eq[1], and_1_out, and_2_out);
  and and_2 (and_2_out, ~comparator_4_eq, comparator_5_eq);  // AND_Gate
  or or_3 (or_3_out, comparator_5_eq, comparator_6_eq, comparator_3_eq);
  not not_1 (not_1_out, RegSelA);
  Multiplexer #(.width(32), .enable("false")) multiplexer_3 (
    .in0(idrr_ex_buffer_1_pc_2), .in1(idrr_ex_buffer_1_a_2), .out(multiplexer_3_out), .sel(not_1_out));
  Multiplexer #(.width(32), .enable("false")) multiplexer_4 (
    .in0(idrr_ex_buffer_1_bout), .in1(idrr_ex_buffer_1_imm_2), .out(multiplexer_4_out), .sel(RegSelB));
  Multiplexer #(.width(2), .enable("false")) multiplexer_5 (
    .in0(comparator_2_eq), .in1(2'b11), .out(Condition), .sel(Stall));
  ROM #(.addrWidth(4), .dataWidth(7)) rom_1 (
    .addr(EX_Opcode), .data({rom_1_data, Func, RegSelB, RegSelA}));  // open: sel
  ALU alu_1 (.Func(Func), .A(multiplexer_3_out), .B(multiplexer_4_out), .Output(EX_Result));
  Adder #(.width(32)) adder_2 (.a(ID_PC), .b(ID_Imm), .out(Branch));  // open: cin, cout
  EX_MEM_Buffer ex_mem_buffer_1 (
    .Opcode(EX_Opcode), .Rx(EX_Rx), .Control(rom_1_data), .Result(EX_Result), .B(idrr_ex_buffer_1_bout),
    .Opcode_2(MEM_Opcode), .Rx_2(MEM_Rx),
    .Control_2({ex_mem_buffer_1_control_2[2], WrMEM, ex_mem_buffer_1_control_2[0]}),
    .Result_2(ex_mem_buffer_1_result_2), .B_2(ex_mem_buffer_1_b_2), .Clock(Clock), .Reset(1'b0));
  Comparator #(.width(4)) comparator_7 (.a(IF_Opcode), .b(4'b0011), .eq(comparator_7_eq));  // open: gt, lt
  Comparator #(.width(32)) comparator_8 (.a(ID_A), .b(ID_B), .eq(comparator_8_eq));  // open: gt, lt
  Comparator #(.width(4)) comparator_9 (.a(ID_Opcode), .b(4'b0011), .eq(comparator_9_eq));  // open: gt, lt
  and and_3 (Save, comparator_7_eq, comparator_8_eq, comparator_9_eq);
  Dual_Ported_Register_File dual_ported_register_file_1 (
    .CLK(Clock), .WrREGNO(WB_Rx), .RdREGNO1(ID_Ry), .RdREGNO2(ID_Rz), .INPUT(WB_Result), .OUT1(OUT1),
    .OUT2(OUT2), .WrEN(WB_Control));
  assign controlled_buffer_1_out = WrMEM ? ex_mem_buffer_1_b_2 : 32'bz;  // Controlled_Buffer controlled_buffer_1
  not not_2 (not_2_out, WrMEM);
  Multiplexer #(.width(32), .enable("false")) multiplexer_6 (
    .in0(ex_mem_buffer_1_result_2), .in1(controlled_buffer_1_out), .out(MEM_Result),
    .sel(ex_mem_buffer_1_control_2[0]));
  RAM #(.addrWidth(24), .dataWidth(32)) ram_2 (
    .addr(ex_mem_buffer_1_result_2[23:0]), .data(controlled_buffer_1_out), .clk(Clock), .ld(not_2_out),
    .clr(1'b0));  // open: sel
  MEM_WB_Buffer mem_wb_buffer_1 (
    .Opcode(MEM_Opcode), .Rx(MEM_Rx), .Control(ex_mem_buffer_1_control_2[2]), .Result(MEM_Result),
    .Opcode_2(WB_Opcode), .Rx_2(WB_Rx), .Control_2(WB_Control), .Result_2(WB_Result), .Clock(Clock),
    .Reset(1'b0));

  // Other names for the same wires on the sheet: Jump[31:0] = ID_A

  // Notes on the sheet:
  //   contents of rom_1 (hex, n*v repeats v):
  //   40 42 48 0 4d 52 43 22 46
endmodule

module Dual_Ported_Register_File (
  input  CLK,
  input  WrEN,
  input  [3:0] WrREGNO,
  input  [3:0] RdREGNO1,
  input  [3:0] RdREGNO2,
  input  [31:0] INPUT,
  output [31:0] OUT1,
  output [31:0] OUT2
);

  wire En_a0, En_a1, En_a2, En_at, En_fp, En_k0, En_ra, En_s0, En_s1, En_s2, En_sp, En_t0, En_t1, En_t2,
       En_v0;
  wire [31:0] a0, a1, a2, at, fp, k0, ra, s0, s1, s2, sp, t0, t1, t2, v0, zero;

  Decoder #(.select(4), .disabled(0)) decoder_1 (
    .out1(En_at), .out2(En_v0), .out3(En_a0), .out4(En_a1), .out5(En_a2), .out6(En_t0), .out7(En_t1),
    .out8(En_t2), .out9(En_s0), .out10(En_s1), .out11(En_s2), .out12(En_k0), .out13(En_sp), .out14(En_fp),
    .out15(En_ra), .sel(WrREGNO), .en(WrEN));  // open: out0
  Register #(.width(32)) u_zero (.D(INPUT), .en(1'b0), .Q(zero), .clk(CLK));  // open: clr
  Register #(.width(32)) u_at (.D(INPUT), .en(En_at), .Q(at), .clk(CLK));  // open: clr
  Register #(.width(32)) u_v0 (.D(INPUT), .en(En_v0), .Q(v0), .clk(CLK));  // open: clr
  Register #(.width(32)) u_a0 (.D(INPUT), .en(En_a0), .Q(a0), .clk(CLK));  // open: clr
  Register #(.width(32)) u_a1 (.D(INPUT), .en(En_a1), .Q(a1), .clk(CLK));  // open: clr
  Register #(.width(32)) u_a2 (.D(INPUT), .en(En_a2), .Q(a2), .clk(CLK));  // open: clr
  Register #(.width(32)) u_t0 (.D(INPUT), .en(En_t0), .Q(t0), .clk(CLK));  // open: clr
  Register #(.width(32)) u_t1 (.D(INPUT), .en(En_t1), .Q(t1), .clk(CLK));  // open: clr
  Multiplexer #(.select(4), .width(32), .disabled(0), .enable("false")) multiplexer_1 (
    .in0(zero), .in1(at), .in2(v0), .in3(a0), .in4(a1), .in5(a2), .in6(t0), .in7(t1), .in8(t2), .in9(s0),
    .in10(s1), .in11(s2), .in12(k0), .in13(sp), .in14(fp), .in15(ra), .out(OUT2), .sel(RdREGNO2));
  Register #(.width(32)) u_t2 (.D(INPUT), .en(En_t2), .Q(t2), .clk(CLK));  // open: clr
  Register #(.width(32)) u_s0 (.D(INPUT), .en(En_s0), .Q(s0), .clk(CLK));  // open: clr
  Register #(.width(32)) u_s1 (.D(INPUT), .en(En_s1), .Q(s1), .clk(CLK));  // open: clr
  Register #(.width(32)) u_s2 (.D(INPUT), .en(En_s2), .Q(s2), .clk(CLK));  // open: clr
  Register #(.width(32)) u_k0 (.D(INPUT), .en(En_k0), .Q(k0), .clk(CLK));  // open: clr
  Register #(.width(32)) u_sp (.D(INPUT), .en(En_sp), .Q(sp), .clk(CLK));  // open: clr
  Register #(.width(32)) u_fp (.D(INPUT), .en(En_fp), .Q(fp), .clk(CLK));  // open: clr
  Register #(.width(32)) u_ra (.D(INPUT), .en(En_ra), .Q(ra), .clk(CLK));  // open: clr
  Multiplexer #(.select(4), .width(32), .disabled(0), .enable("false")) multiplexer_2 (
    .in0(zero), .in1(at), .in2(v0), .in3(a0), .in4(a1), .in5(a2), .in6(t0), .in7(t1), .in8(t2), .in9(s0),
    .in10(s1), .in11(s2), .in12(k0), .in13(sp), .in14(fp), .in15(ra), .out(OUT1), .sel(RdREGNO1));

  // Notes on the sheet:
  //   MODIFY AT YOUR OWN RISK
endmodule

module IF_IDRR_Buffer (
  input  Clock,
  input  Reset,
  input  Stall,
  input  [31:0] PC,
  input  [31:0] IR,
  output [31:0] PC_2,
  output [31:0] IR_2
);

  wire [31:0] multiplexer_1_out, multiplexer_2_out;

  Multiplexer #(.width(32), .enable("false")) multiplexer_1 (
    .in0(PC), .in1({32{1'b0}}), .out(multiplexer_1_out), .sel(Stall));
  Multiplexer #(.width(32), .enable("false")) multiplexer_2 (
    .in0(IR), .in1({32{1'b0}}), .out(multiplexer_2_out), .sel(Stall));
  Register #(.width(32)) u_PC (.D(multiplexer_1_out), .Q(PC_2), .clk(Clock), .clr(Reset));  // open: en
  Register #(.width(32)) u_IR (.D(multiplexer_2_out), .Q(IR_2), .clk(Clock), .clr(Reset));  // open: en
endmodule

module IDRR_EX_Buffer (
  input  Clock,
  input  Reset,
  input  Stall,
  input  [3:0] Opcode,
  input  [3:0] Rx,
  input  [31:0] PC,
  input  [31:0] Imm,
  input  [31:0] A,
  input  [31:0] Bin,
  output [3:0] Opcode_2,
  output [3:0] Rx_2,
  output [31:0] PC_2,
  output [31:0] Imm_2,
  output [31:0] A_2,
  output [31:0] Bout
);

  wire [3:0] multiplexer_1_out, multiplexer_2_out;
  wire [31:0] multiplexer_3_out, multiplexer_4_out, multiplexer_5_out, multiplexer_6_out;

  Multiplexer #(.width(4), .enable("false")) multiplexer_1 (
    .in0(Opcode), .in1(4'b0000), .out(multiplexer_1_out), .sel(Stall));
  Multiplexer #(.width(4), .enable("false")) multiplexer_2 (
    .in0(Rx), .in1(4'b0000), .out(multiplexer_2_out), .sel(Stall));
  Multiplexer #(.width(32), .enable("false")) multiplexer_3 (
    .in0(PC), .in1({32{1'b0}}), .out(multiplexer_3_out), .sel(Stall));
  Multiplexer #(.width(32), .enable("false")) multiplexer_4 (
    .in0(Imm), .in1({32{1'b0}}), .out(multiplexer_4_out), .sel(Stall));
  Multiplexer #(.width(32), .enable("false")) multiplexer_5 (
    .in0(A), .in1({32{1'b0}}), .out(multiplexer_5_out), .sel(Stall));
  Multiplexer #(.width(32), .enable("false")) multiplexer_6 (
    .in0(Bin), .in1({32{1'b0}}), .out(multiplexer_6_out), .sel(Stall));
  Register #(.width(4)) u_Opcode (.D(multiplexer_1_out), .Q(Opcode_2), .clk(Clock), .clr(Reset));  // open: en
  Register #(.width(4)) u_Rx (.D(multiplexer_2_out), .Q(Rx_2), .clk(Clock), .clr(Reset));  // open: en
  Register #(.width(32)) u_PC (.D(multiplexer_3_out), .Q(PC_2), .clk(Clock), .clr(Reset));  // open: en
  Register #(.width(32)) u_Imm (.D(multiplexer_4_out), .Q(Imm_2), .clk(Clock), .clr(Reset));  // open: en
  Register #(.width(32)) u_A (.D(multiplexer_5_out), .Q(A_2), .clk(Clock), .clr(Reset));  // open: en
  Register #(.width(32)) B (.D(multiplexer_6_out), .Q(Bout), .clk(Clock), .clr(Reset));  // open: en
endmodule

module EX_MEM_Buffer (
  input  Clock,
  input  Reset,
  input  [3:0] Opcode,
  input  [3:0] Rx,
  input  [2:0] Control,
  input  [31:0] Result,
  input  [31:0] B,
  output [3:0] Opcode_2,
  output [3:0] Rx_2,
  output [2:0] Control_2,
  output [31:0] Result_2,
  output [31:0] B_2
);

  Register #(.width(4)) u_Opcode (.D(Opcode), .Q(Opcode_2), .clk(Clock), .clr(Reset));  // open: en
  Register #(.width(4)) u_Rx (.D(Rx), .Q(Rx_2), .clk(Clock), .clr(Reset));  // open: en
  Register #(.width(3)) u_Control (.D(Control), .Q(Control_2), .clk(Clock), .clr(Reset));  // open: en
  Register #(.width(32)) u_Result (.D(Result), .Q(Result_2), .clk(Clock), .clr(Reset));  // open: en
  Register #(.width(32)) u_B (.D(B), .Q(B_2), .clk(Clock), .clr(Reset));  // open: en
endmodule

module MEM_WB_Buffer (
  input  Clock,
  input  Reset,
  input  [3:0] Opcode,
  input  [3:0] Rx,
  input  Control,
  input  [31:0] Result,
  output [3:0] Opcode_2,
  output [3:0] Rx_2,
  output Control_2,
  output [31:0] Result_2
);

  Register #(.width(4)) u_Opcode (.D(Opcode), .Q(Opcode_2), .clk(Clock), .clr(Reset));  // open: en
  Register #(.width(4)) u_Rx (.D(Rx), .Q(Rx_2), .clk(Clock), .clr(Reset));  // open: en
  Register #(.width(1)) u_Control (.D(Control), .Q(Control_2), .clk(Clock), .clr(Reset));  // open: en
  Register #(.width(32)) u_Result (.D(Result), .Q(Result_2), .clk(Clock), .clr(Reset));  // open: en
endmodule

module Data_Forward_Unit (
  input  [31:0] WB_Data,
  input  [31:0] MEM_Data,
  input  [31:0] ID_Data,
  input  [31:0] EX_Data,
  input  [3:0] ID_SR,
  input  [3:0] EX_DR,
  input  [3:0] MEM_DR,
  input  [3:0] WB_DR,
  input  [3:0] EX_Opcode,
  input  [3:0] MEM_Opcode,
  input  [3:0] WB_Opcode,
  output [31:0] Result,
  output Stall
);

  wire EX_Forward, MEM_Forward, WB_Forward;
  wire [0:0] comparator_2_eq, comparator_3_eq;
  wire [1:1] comparator_1_eq, multiplexer_2_out, multiplexer_3_out;

  Comparator #(.width(4)) comparator_1 (.a(ID_SR), .b(EX_DR), .eq(comparator_1_eq[1]));  // open: gt, lt
  Comparator #(.width(4)) comparator_2 (.a(ID_SR), .b(MEM_DR), .eq(comparator_2_eq[0]));  // open: gt, lt
  Comparator #(.width(4)) comparator_3 (.a(ID_SR), .b(WB_DR), .eq(comparator_3_eq[0]));  // open: gt, lt
  Multiplexer #(.select(4), .width(2), .enable("false")) multiplexer_1 (
    .in0({1'b0, comparator_1_eq[1]}), .in1({1'b0, comparator_1_eq[1]}), .in2({1'b0, comparator_1_eq[1]}),
    .in3(2'b00), .in4({1'b0, comparator_1_eq[1]}), .in5({comparator_1_eq[1], 1'b0}),
    .in6({1'b0, comparator_1_eq[1]}), .in7(2'b00), .in8({1'b0, comparator_1_eq[1]}), .in9(2'b00),
    .in10(2'b00), .in11(2'b00), .in12(2'b00), .in13(2'b00), .in14(2'b00), .in15(2'b00),
    .out({Stall, EX_Forward}), .sel(EX_Opcode));
  Multiplexer #(.select(4), .width(2), .enable("false")) multiplexer_2 (
    .in0({1'b0, comparator_2_eq[0]}), .in1({1'b0, comparator_2_eq[0]}), .in2({1'b0, comparator_2_eq[0]}),
    .in3(2'b00), .in4({1'b0, comparator_2_eq[0]}), .in5({1'b0, comparator_2_eq[0]}),
    .in6({1'b0, comparator_2_eq[0]}), .in7(2'b00), .in8({1'b0, comparator_2_eq[0]}), .in9(2'b00),
    .in10(2'b00), .in11(2'b00), .in12(2'b00), .in13(2'b00), .in14(2'b00), .in15(2'b00),
    .out({multiplexer_2_out[1], MEM_Forward}), .sel(MEM_Opcode));
  Multiplexer #(.select(4), .width(2), .enable("false")) multiplexer_3 (
    .in0({1'b0, comparator_3_eq[0]}), .in1({1'b0, comparator_3_eq[0]}), .in2({1'b0, comparator_3_eq[0]}),
    .in3(2'b00), .in4({1'b0, comparator_3_eq[0]}), .in5({1'b0, comparator_3_eq[0]}),
    .in6({1'b0, comparator_3_eq[0]}), .in7(2'b00), .in8({1'b0, comparator_3_eq[0]}), .in9(2'b00),
    .in10(2'b00), .in11(2'b00), .in12(2'b00), .in13(2'b00), .in14(2'b00), .in15(2'b00),
    .out({multiplexer_3_out[1], WB_Forward}), .sel(WB_Opcode));
  Multiplexer #(.select(3), .width(32), .enable("false")) multiplexer_4 (
    .in0(ID_Data), .in1(WB_Data), .in2(MEM_Data), .in3(MEM_Data), .in4(EX_Data), .in5(EX_Data),
    .in6(EX_Data), .in7(EX_Data), .out(Result), .sel({EX_Forward, MEM_Forward, WB_Forward}));
endmodule

module ALU (
  input  [1:0] Func,
  input  [31:0] A,
  input  [31:0] B,
  output [31:0] Output
);

  wire [31:0] ADD, NAND, SHIFT, shifter_1_out, shifter_2_out, shifter_3_out;

  Shifter #(.width(32)) shifter_1 (.in(A), .\dist (B[4:0]), .out(shifter_1_out));
  Shifter #(.width(32), .shift("lr")) shifter_2 (.in(A), .\dist (B[4:0]), .out(shifter_2_out));
  Shifter #(.width(32), .shift("ar")) shifter_3 (.in(A), .\dist (B[4:0]), .out(shifter_3_out));
  Multiplexer #(.select(2), .width(32), .disabled(0), .enable("false")) multiplexer_1 (
    .in0(shifter_1_out), .in1(shifter_2_out), .in2(shifter_1_out), .in3(shifter_3_out), .out(SHIFT),
    .sel(B[19:18]));
  Multiplexer #(.select(2), .width(32), .disabled(0), .enable("false")) multiplexer_2 (
    .in0(ADD), .in1(NAND), .in2(SHIFT), .in3(A), .out(Output), .sel(Func));
  Adder #(.width(32)) adder_1 (.a(A), .b(B), .out(ADD));  // open: cin, cout
  assign NAND = ~(A & B);  // NAND_Gate nand_1, 32 bits wide
endmodule
